# Fritzing sketch sketch (saved by Fritzing 0.9.3b)
circuit board: 8.46667cm x 5.64444cm

parts:
  Gizwits_WiFi_Witty_ESP-12F1 = Gizwits WiFi Witty ESP-12F
  J1 = Basic Servo

nets:
  N1: Gizwits_WiFi_Witty_ESP-12F1.REST, Gizwits_WiFi_Witty_ESP-12F1.GPIO16
  N2: Gizwits_WiFi_Witty_ESP-12F1.GPIO12, J1.pulse
  VCC: Gizwits_WiFi_Witty_ESP-12F1.VCC, J1.vcc
  GND: Gizwits_WiFi_Witty_ESP-12F1.GND, J1.gnd
